# Fritzing sketch RTC Pi circuit (saved by Fritzing 0.9.3b)
breadboards: 1

parts:
  IC2 = MCP7940M [package=THT]
  Raspberry_Pi_1 = Raspberry Pi 3 [part_number=RPI-3-V1.2]

nets:
  N1: IC2.0V, Raspberry_Pi_1.GND
  N2: IC2.+V, Raspberry_Pi_1.3v3

custom parts:
  MCP7940M: I2C Real Time Clock
