// Logisim project prac_5_ARNJAM004_WLFJAD001.circ as structural Verilog: 6 circuits, main circuit main
module main (
  input  A0,
  input  A1,
  input  B0,
  input  B1,
  input  F0,
  input  F1,
  input  F2,
  output Cout,
  output Y0,
  output Y1
);

  wire adder_1_s0, adder_1_s1, Bitwise_AND_y0, Bitwise_AND_y1, Bitwise_OR_y0, Bitwise_OR_y1, Divide_0_1_y0,
       Divide_0_1_y1, multiplexer_1_out, multiplexer_2_out, multiplexer_3_out, multiplexer_4_out,
       multiplexer_5_out, multiplexer_6_out, multiplexer_7_out, multiplexer_8_out, Multiply_0_1_y0,
       Multiply_0_1_y1;

  Multiplexer #(.enable("false")) multiplexer_1 (.in0(B1), .in1(1'b0), .out(multiplexer_1_out), .sel(F1));
  Bitwise_AND Bitwise_AND (.A0(A0), .B0(A1), .A1(B0), .B1(B1), .Y0(Bitwise_AND_y0), .Y1(Bitwise_AND_y1));
  Bitwise_OR Bitwise_OR (.A0(A0), .B0(A1), .A1(B0), .B1(B1), .Y0(Bitwise_OR_y0), .Y1(Bitwise_OR_y1));
  Multiply_0_1 Multiply_0_1 (.A1(A1), .A0(A0), .Y1(Multiply_0_1_y1), .Y0(Multiply_0_1_y0));
  Divide_0_1 Divide_0_1 (.A0(A0), .A1(A1), .Y0(Divide_0_1_y0), .Y1(Divide_0_1_y1));
  Multiplexer #(.enable("false")) multiplexer_2 (.in0(B0), .in1(1'b1), .out(multiplexer_2_out), .sel(F1));
  Adder adder_1 (
    .A0(A0), .B0(multiplexer_2_out), .Sel(F0), .A1(A1), .B1(multiplexer_1_out), .S0(adder_1_s0),
    .S1(adder_1_s1), .Cout(Cout));
  Multiplexer #(.enable("false")) multiplexer_3 (
    .in0(Bitwise_AND_y0), .in1(Bitwise_OR_y0), .out(multiplexer_3_out), .sel(F0));
  Multiplexer #(.enable("false")) multiplexer_4 (
    .in0(Bitwise_AND_y1), .in1(Bitwise_OR_y1), .out(multiplexer_4_out), .sel(F0));
  Multiplexer #(.enable("false")) multiplexer_5 (
    .in0(Multiply_0_1_y0), .in1(Divide_0_1_y0), .out(multiplexer_5_out), .sel(F0));
  Multiplexer #(.enable("false")) multiplexer_6 (
    .in0(Multiply_0_1_y1), .in1(Divide_0_1_y1), .out(multiplexer_6_out), .sel(F0));
  Multiplexer #(.enable("false")) multiplexer_7 (
    .in0(multiplexer_5_out), .in1(multiplexer_3_out), .out(multiplexer_7_out), .sel(F0));
  Multiplexer #(.enable("false")) multiplexer_8 (
    .in0(multiplexer_6_out), .in1(multiplexer_4_out), .out(multiplexer_8_out), .sel(F0));
  Multiplexer #(.enable("false")) multiplexer_9 (.in0(adder_1_s0), .in1(multiplexer_7_out), .out(Y0), .sel(F2));
  Multiplexer #(.enable("false")) multiplexer_10 (.in0(adder_1_s1), .in1(multiplexer_8_out), .out(Y1), .sel(F2));
endmodule

module Adder (
  input  A0,
  input  B0,
  input  Sel,
  input  A1,
  input  B1,
  output S0,
  output S1,
  output Cout
);

  wire adder_1_cout, xor_1_out, xor_2_out;

  xor xor_1 (xor_1_out, B0, Sel);
  xor xor_2 (xor_2_out, B1, Sel);
  Adder_part #(.width(1)) adder_1 (.a(A0), .b(xor_1_out), .out(S0), .cin(Sel), .cout(adder_1_cout));
  Adder_part #(.width(1)) adder_2 (.a(A1), .b(xor_2_out), .out(S1), .cin(adder_1_cout), .cout(Cout));
endmodule

module Bitwise_AND (
  input  A0,
  input  B0,
  input  A1,
  input  B1,
  output Y0,
  output Y1
);

  and and_1 (Y0, A0, B0);
  and and_2 (Y1, A1, B1);
endmodule

module Bitwise_OR (
  input  A0,
  input  B0,
  input  A1,
  input  B1,
  output Y0,
  output Y1
);

  or or_1 (Y0, A0, B0);
  or or_2 (Y1, A1, B1);
endmodule

module Multiply_0_1 (
  input  A1,
  input  A0,
  output Y1,
  output Y0
);

  Multiplexer #(.enable("false")) multiplexer_1 (.in0(A1), .in1(A0), .out(Y1), .sel(1'b1));
  Multiplexer #(.enable("false")) multiplexer_2 (.in0(A0), .in1(1'b0), .out(Y0), .sel(1'b1));
endmodule

module Divide_0_1 (
  input  A0,
  input  A1,
  output Y0,
  output Y1
);

  Multiplexer #(.enable("false")) multiplexer_1 (.in0(A0), .in1(A1), .out(Y0), .sel(1'b1));
  Multiplexer #(.enable("false")) multiplexer_2 (.in0(A1), .in1(1'b0), .out(Y1), .sel(1'b1));
endmodule
